# Fritzing sketch KISSRtwo (saved by Fritzing 0.9.9b)
circuit board: 5.35693cm x 4.3164cm
breadboards: 1

parts:
  Part6 = Radiometrix NTX2  # not connected
  J2 = female pin header, 4 pins [form="♀ (female)" part_number="ntx2 4-pin"]
  J3 = female pin header, 2 pins [form="♀ (female)" part_number="pro-mini a4/5"]
  J7 = female pin header, 4 pins [form="♀ (female)" part_number="i2c 4"]
  J8 = female pin header, 4 pins [form="♀ (female)" part_number="i2c 3"]
  J10 = female pin header, 4 pins [form="♀ (female)" part_number="i2c 1"]
  JP1 = Header 2 [package=jst-2-pth-kit]
  J11 = female pin header, 4 pins [form="♀ (female)" part_number="pro-mini rx/tx"]
  Part8 = Arduino Pro Mini v13  # not connected
  J1 = female pin header, 7 pins [form="♀ (female)"]
  J12 = female pin header, 6 pins [form="♀ (female)"]
  J13 = female pin header, 4 pins [form="♀ (female)" part_number=ft232]
  J4 = female pin header, 5 pins [form="♀ (female)"]
  J16 = female pin header, 3 pins [form="♀ (female)"]
  S2 = Toggle Switch [package=THT]
  R4 = Resistor [tolerance=±5% resistance=220 power=0.25 package=THT]
  J18 = female pin header, 2 pins [form="♀ (female)" part_number="pro-mini a4/5"]
  R5 = Resistor [tolerance=±5% resistance=220 power=0.25 package=THT]
  J19 = female pin header, 2 pins [form="♀ (female)" part_number="pro-mini a4/5"]
  J14 = female pin header, 3 pins [form="♀ (female)" part_number="ntx2 3-pin"]
  J22 = female pin header, 2 pins [form="♀ (female)" part_number="pro-mini a4/5"]
  J23 = female pin header, 2 pins [form="♀ (female)" part_number="pro-mini a4/5"]
  J6 = female pin header, 5 pins [form="♀ (female)"]
  J$6 = SMA Antenna Connector [package=sma-edge]

nets:
  N1: J2.pin1, J4.pin5
  N2: J2.pin2, J7.pin2, J8.pin2, J10.pin2, J1.pin6, J13.pin1, J16.pin3, S2.L2, J23.pin1, J6.pin2
  N3: J2.pin3, J14.pin1, J14.pin3, J$6.GND
  N4: J2.pin4, J12.pin6
  N5: J3.pin1, J7.pin3, J8.pin3, J10.pin3
  N6: J3.pin2, J7.pin4, J8.pin4, J10.pin4
  N7: JP1.2, J22.pin1
  N8: J11.pin1, J1.pin3
  N9: J11.pin2, J1.pin2
  N10: J12.pin2, J13.pin2, J6.pin3
  N11: J12.pin3, J13.pin3, J6.pin4
  N12: J12.pin4, J6.pin5
  N13: J12.pin5, R5.Pin_0
  N14: J4.pin1, J16.pin2
  N15: J4.pin3, J18.pin2
  N16: J4.pin4, S2.COM
  N17: S2.L1, R4.Pin_1
  N18: R5.Pin_1, J19.pin2
  N19: J14.pin2, J$6.SIGNAL

notes:
  VCC
  KISSR:two
  GND
  RAW
  TX
  RX
  D6
  D8
  D7
  GRN
  D12
  EN
  TXD
  D9
  SCL
  SDA
  OpenLog
  I2C BUS
  D10
  OUT
  GPS MODULE
  FT232R
  NTX2B
  POWER
  TMP36
  +
  -
  A0
  LED
  FLIGHT
  GROUND
  SIG
  CAMERA
  SWITCH
  MODE
  A3

custom parts:
  Radiometrix NTX2: The NTX2 transmitter and NRX2 receiver offer a low power, reliable data link in a Radiometrix SIL standard pin out and foot print.
